// Logisim project cpu.circ as structural Verilog: 14 circuits, main circuit main
// CPU
module main (
  input  [31:0] RS_READ_VALUE,
  input  [31:0] RI_READ_VALUE,
  input  [31:0] RD_READ_VALUE,
  input  [31:0] JC_READ_VALUE,
  input  [31:0] INSTRUCTION,
  input  CLOCK,
  output [4:0] RS,
  output [4:0] RI,
  output [4:0] RD,
  output [31:0] RD_WRITE_VALUE,
  output RD_WRITE_ENABLE,
  output [23:0] FETCH_ADDRESS
);

  wire ADDR_SELECT, I, JAL, MEM_WRITE, WORD_MODE;
  wire [1:0] RD_SELECT;
  wire [2:0] JC_t;
  wire [3:0] ALU_CONTROL, OP;
  wire [4:0] u_decoder_1_rd;
  wire [16:0] IMM;
  wire [23:0] ADDR, bit_extender_5_out, NEXT_PC, PC_IN;
  wire [24:0] bit_extender_1_out;
  wire [31:0] ALU_RESULT, bit_extender_2_out, bit_extender_3_out, bit_extender_4_out, MEM_READ,
       multiplexer_4_out, RI_IMM;

  Register #(.width(24)) register_1 (.D(PC_IN), .Q(FETCH_ADDRESS), .clk(CLOCK));  // open: en, clr
  u_DECODER u_decoder_1 (
    .INSTRUCTION_MEMORY_INPUT(INSTRUCTION), .IMMEDIATE(IMM), .ADDRESS(ADDR), .RD(u_decoder_1_rd), .JC(JC_t),
    .RS(RS), .OP(OP), .RI(RI), .I(I));
  Multiplexer #(.width(5), .enable("false")) multiplexer_1 (.in0(u_decoder_1_rd), .in1(5'b00110), .out(RD), .sel(JAL));
  u_ALU u_alu_1 (.ALU_X(RS_READ_VALUE), .ALU_Y(RI_IMM), .ALU_CONTROL(ALU_CONTROL), .ALU_RESULT(ALU_RESULT));
  Bit_Extender #(.in_width(32), .out_width(25)) bit_extender_1 (.in(ALU_RESULT), .out(bit_extender_1_out));
  assign bit_extender_2_out = {{8{1'b0}}, NEXT_PC};  // Bit_Extender bit_extender_2
  assign bit_extender_3_out = {{15{IMM[16]}}, IMM};  // Bit_Extender bit_extender_3
  assign bit_extender_4_out = {{8{1'b0}}, ADDR};  // Bit_Extender bit_extender_4
  u_CONTROLLER u_controller_1 (
    .OPCODE(OP), .JC(JC_t), .I(I), .JC_2(JC_READ_VALUE), .ALU_CONTROL(ALU_CONTROL), .ADDR_SEL(ADDR_SELECT),
    .RD_SELECT(RD_SELECT), .WORD_MODE(WORD_MODE), .MEM_WRITE(MEM_WRITE), .EN_WRITE(RD_WRITE_ENABLE), .JAL(JAL));
  Multiplexer #(.select(2), .width(32), .enable("false")) multiplexer_2 (
    .in0(MEM_READ), .in1(ALU_RESULT), .in2(bit_extender_2_out), .out(RD_WRITE_VALUE), .sel(RD_SELECT));  // open: in3
  Multiplexer #(.width(32), .enable("false")) multiplexer_3 (
    .in0(RI_READ_VALUE), .in1(bit_extender_3_out), .out(RI_IMM), .sel(I));
  Bit_Extender #(.in_width(32), .out_width(24)) bit_extender_5 (.in(multiplexer_4_out), .out(bit_extender_5_out));
  Multiplexer #(.width(32), .enable("false")) multiplexer_4 (
    .in0(RI_READ_VALUE), .in1(bit_extender_4_out), .out(multiplexer_4_out), .sel(I));
  u_MEM u_mem_1 (
    .ADDRESS(bit_extender_1_out), .WORD_MODE(WORD_MODE), .MEM_WRITE(MEM_WRITE), .DATA_IN(RD_READ_VALUE),
    .CLOCK(CLOCK), .DATA_OUT(MEM_READ));
  Adder #(.width(24)) adder_1 (.a(FETCH_ADDRESS), .b(24'h1), .out(NEXT_PC));  // open: cin, cout
  Multiplexer #(.width(24), .enable("false")) multiplexer_5 (
    .in0(NEXT_PC), .in1(bit_extender_5_out), .out(PC_IN), .sel(ADDR_SELECT));

  // Other names for the same wires on the sheet: CLK = CLOCK; EN_WRITE = RD_WRITE_ENABLE; JC[31:0] = JC_READ_VALUE;
  //   PC_OUT[23:0] = FETCH_ADDRESS; RD_t[31:0] = RD_READ_VALUE; RD_WRITE_VAL[31:0] = RD_WRITE_VALUE;
  //   RI_t[31:0] = RI_READ_VALUE; RS_t[31:0] = RS_READ_VALUE

  // Notes on the sheet:
  //   INPUTS/OUTPUTS
  //   INSTRUCTION MEMORY
  //   CONTROLLER
  //   TO REG FILE
  //   RI/IMM SELECTOR
endmodule

module u_ALU (
  input  [31:0] ALU_X,
  input  [31:0] ALU_Y,
  input  [3:0] ALU_CONTROL,
  output [31:0] ALU_RESULT
);

  wire CMP0, CMP1, CMP2;
  wire [4:0] X5;
  wire [31:0] ADD, AND, DIV, MUL, OR, REV, SLA, SRA, STU, SUB, XOR;

  // Probe on ALU_X
  // Probe on ALU_Y
  u_SLA u_sla_1 (.INPUT(ALU_X), .SHAMT(X5), .OUTPUT(SLA));
  Shifter #(.width(32), .shift("ar")) shifter_1 (.in(ALU_X), .\dist (X5), .out(SRA));
  u_REV u_rev_1 (.INPUT(ALU_X), .REVERSE_AMOUNT(X5), .OUTPUT(REV));
  Comparator #(.width(32)) comparator_1 (.a(ALU_X), .b({32{1'b0}}), .gt(CMP0), .eq(CMP1), .lt(CMP2));
  u_STU u_stu_1 (.INPUT_A(ALU_X), .INPUT_B(ALU_Y), .OUTPUT(STU));
  assign AND = ALU_X & ALU_Y;  // AND_Gate and_1, 32 bits wide
  assign OR = ALU_X | ALU_Y;  // OR_Gate or_1, 32 bits wide
  assign XOR = ALU_X ^ ALU_Y;  // XOR_Gate xor_1, 32 bits wide
  Adder #(.width(32)) adder_1 (.a(ALU_X), .b(ALU_Y), .out(ADD), .cin(1'b0));  // open: cout
  Subtractor #(.width(32)) subtractor_1 (.a(ALU_X), .b(ALU_Y), .out(SUB), .bin(1'b0));  // open: bout
  Multiplier #(.width(32)) multiplier_1 (.a(ALU_X), .b(ALU_Y), .out(MUL), .cin({32{1'b0}}));  // open: cout
  u_DIV u_div_1 (.INPUT_A(ALU_X), .INPUT_B(ALU_Y), .POSITIVE___X(CMP0), .NEGATIVE___X(CMP2), .OUTPUT(DIV));
  Bit_Extender #(.in_width(32), .out_width(5)) bit_extender_1 (.in(ALU_Y), .out(X5));
  // Probe on ALU_RESULT
  Multiplexer #(.select(4), .width(32), .enable("false")) multiplexer_1 (
    .in0(SLA), .in1(SRA), .in2(AND), .in3(OR), .in4(REV), .in5(XOR), .in6(ADD), .in7(SUB), .in8(MUL),
    .in9(DIV), .in10(ADD), .in11(ADD), .in12(ADD), .in13(ADD), .in14(STU), .in15({32{1'b0}}),
    .out(ALU_RESULT), .sel(ALU_CONTROL));

  // Other names for the same wires on the sheet: CTRL[3:0] = ALU_CONTROL; OUT[31:0] = ALU_RESULT; X[31:0] = ALU_X;
  //   Y[31:0] = ALU_Y

  // Notes on the sheet:
  //   COMPUTE ALL POSSIBLE OPERATIONS
  //   SELECT THE REQUESTED RESULT
endmodule

// Data Memory
module u_MEM (
  input  [24:0] ADDRESS,
  input  WORD_MODE,
  input  MEM_WRITE,
  input  [31:0] DATA_IN,
  input  CLOCK,
  output [31:0] DATA_OUT
);

  wire and_1_out, and_3_out, and_4_out, and_5_out, not_1_out, not_2_out, not_3_out, not_4_out, ODD, or_1_out,
       or_2_out;
  wire [15:0] E_OUT, multiplexer_2_out, multiplexer_3_out, O_OUT, STORE_E, STORE_O;
  wire [23:0] adder_1_out, SUB_ADDR, SUB_E_ADDR;
  wire [24:0] and_2_out, shifter_1_out;
  wire [31:0] bit_extender_3_out, multiplexer_5_out;

  Multiplexer #(.width(16), .enable("false")) multiplexer_1 (
    .in0(DATA_IN[15:0]), .in1(DATA_IN[31:16]), .out(STORE_E), .sel(and_1_out));
  and and_1 (and_1_out, WORD_MODE, ODD);
  Bit_Extender #(.in_width(25), .out_width(1)) bit_extender_1 (.in(and_2_out), .out(ODD));
  assign and_2_out = ADDRESS & 25'h1;  // AND_Gate and_2, 25 bits wide
  Adder #(.width(24)) adder_1 (.a(SUB_ADDR), .b(24'h1), .out(adder_1_out));  // open: cin, cout
  Multiplexer #(.width(16), .enable("false")) multiplexer_2 (
    .in0(E_OUT), .in1(O_OUT), .out(multiplexer_2_out), .sel(ODD));
  Multiplexer #(.width(16), .enable("false")) multiplexer_3 (
    .in0(O_OUT), .in1(E_OUT), .out(multiplexer_3_out), .sel(ODD));
  Bit_Extender #(.in_width(25), .out_width(24)) bit_extender_2 (.in(shifter_1_out), .out(SUB_ADDR));
  Shifter #(.width(25), .shift("ar")) shifter_1 (.in(ADDRESS), .\dist (5'b00001), .out(shifter_1_out));
  Multiplexer #(.width(24), .enable("false")) multiplexer_4 (
    .in0(SUB_ADDR), .in1(adder_1_out), .out(SUB_E_ADDR), .sel(and_1_out));
  assign bit_extender_3_out = {{16{multiplexer_2_out[15]}}, multiplexer_2_out};  // Bit_Extender bit_extender_3
  not not_1 (not_1_out, MEM_WRITE);
  and and_3 (and_3_out, MEM_WRITE, or_1_out);
  or or_1 (or_1_out, not_2_out, WORD_MODE);
  Multiplexer #(.width(32), .enable("false")) multiplexer_5 (
    .in0(bit_extender_3_out), .in1({multiplexer_3_out, multiplexer_2_out}), .out(multiplexer_5_out),
    .sel(WORD_MODE));
  RAM #(.addrWidth(24), .dataWidth(16), .bus("separate")) ram_1 (
    .addr(SUB_E_ADDR), .din(STORE_E), .data(E_OUT), .str(and_3_out), .clk(CLOCK), .ld(not_1_out));  // open: sel, clr
  not not_2 (not_2_out, ODD);
  Multiplexer #(.width(16), .enable("false")) multiplexer_6 (
    .in0(DATA_IN[15:0]), .in1(DATA_IN[31:16]), .out(STORE_O), .sel(and_4_out));
  and and_4 (and_4_out, WORD_MODE, not_3_out);
  Multiplexer #(.width(32), .enable("false")) multiplexer_7 (
    .in0(multiplexer_5_out), .in1({32{1'b0}}), .out(DATA_OUT), .sel(MEM_WRITE));
  not not_3 (not_3_out, ODD);
  and and_5 (and_5_out, MEM_WRITE, or_2_out);
  RAM #(.addrWidth(24), .dataWidth(16), .bus("separate")) ram_2 (
    .addr(SUB_ADDR), .din(STORE_O), .data(O_OUT), .str(and_5_out), .clk(CLOCK), .ld(not_4_out));  // open: sel, clr
  not not_4 (not_4_out, MEM_WRITE);
  or or_2 (or_2_out, ODD, WORD_MODE);

  // Other names for the same wires on the sheet: CLK = CLOCK; D_OUT[31:0] = DATA_OUT;
  //   LOWER_HALF[15:0] = DATA_IN[15:0]; UPPER_HALF[15:0] = DATA_IN[31:16]; WDM = WORD_MODE; WRITE = MEM_WRITE

  // Notes on the sheet:
  //   ODD/EVEN
  //   Feel free to use this component, or not, however you want!
  //   You might use the word mode input to differentiate LW/SW from LH/SH.
  //   24-BIT CONVERTER
  //   However, you *SHOULD* use 2 RAM modules, one for even addresses and one for odd addresses.
endmodule

module u_REV (
  input  [31:0] INPUT,
  input  [4:0] REVERSE_AMOUNT,
  output [31:0] OUTPUT
);

  wire [31:0] u_rev_sub0_1_output, u_rev_sub1_1_output, u_rev_sub2_1_output, u_rev_sub3_1_output;

  u_REV_SUB0 u_rev_sub0_1 (.INPUT(INPUT), .SELECT(REVERSE_AMOUNT[0]), .OUTPUT(u_rev_sub0_1_output));
  u_REV_SUB1 u_rev_sub1_1 (.INPUT(u_rev_sub0_1_output), .SELECT(REVERSE_AMOUNT[1]), .OUTPUT(u_rev_sub1_1_output));
  u_REV_SUB2 u_rev_sub2_1 (.INPUT(u_rev_sub1_1_output), .SELECT(REVERSE_AMOUNT[2]), .OUTPUT(u_rev_sub2_1_output));
  u_REV_SUB3 u_rev_sub3_1 (.INPUT(u_rev_sub2_1_output), .SELECT(REVERSE_AMOUNT[3]), .OUTPUT(u_rev_sub3_1_output));
  u_REV_SUB4 u_rev_sub4_1 (.INPUT(u_rev_sub3_1_output), .SELECT(REVERSE_AMOUNT[4]), .OUTPUT(OUTPUT));

  // Notes on the sheet:
  //   Feel free to use this component, or not, however you want!
endmodule

// 0
module u_REV_SUB0 (
  input  [31:0] INPUT,
  input  SELECT,
  output [31:0] OUTPUT
);

  Multiplexer #(.width(32), .enable("false")) multiplexer_1 (
    .in0(INPUT),
    .in1({INPUT[30], INPUT[31], INPUT[28], INPUT[29], INPUT[26], INPUT[27], INPUT[24], INPUT[25], INPUT[22], INPUT[23], INPUT[20], INPUT[21], INPUT[18], INPUT[19], INPUT[16], INPUT[17], INPUT[14], INPUT[15], INPUT[12], INPUT[13], INPUT[10], INPUT[11], INPUT[8], INPUT[9], INPUT[6], INPUT[7], INPUT[4], INPUT[5], INPUT[2], INPUT[3], INPUT[0], INPUT[1]}),
    .out(OUTPUT), .sel(SELECT));

  // Other names for the same wires on the sheet: FWD[31:0] = INPUT;
  //   REV[31:0] = {INPUT[30], INPUT[31], INPUT[28], INPUT[29], INPUT[26], INPUT[27], INPUT[24], INPUT[25], INPUT[22], INPUT[23], INPUT[20], INPUT[21], INPUT[18], INPUT[19], INPUT[16], INPUT[17], INPUT[14], INPUT[15], INPUT[12], INPUT[13], INPUT[10], INPUT[11], INPUT[8], INPUT[9], INPUT[6], INPUT[7], INPUT[4], INPUT[5], INPUT[2], INPUT[3], INPUT[0], INPUT[1]}
endmodule

// 1
module u_REV_SUB1 (
  input  [31:0] INPUT,
  input  SELECT,
  output [31:0] OUTPUT
);

  Multiplexer #(.width(32), .enable("false")) multiplexer_1 (
    .in0(INPUT),
    .in1({INPUT[29:28], INPUT[31:30], INPUT[25:24], INPUT[27:26], INPUT[21:20], INPUT[23:22], INPUT[17:16], INPUT[19:18], INPUT[13:12], INPUT[15:14], INPUT[9:8], INPUT[11:10], INPUT[5:4], INPUT[7:6], INPUT[1:0], INPUT[3:2]}),
    .out(OUTPUT), .sel(SELECT));

  // Other names for the same wires on the sheet: FWD[31:0] = INPUT;
  //   REV[31:0] = {INPUT[29:28], INPUT[31:30], INPUT[25:24], INPUT[27:26], INPUT[21:20], INPUT[23:22], INPUT[17:16], INPUT[19:18], INPUT[13:12], INPUT[15:14], INPUT[9:8], INPUT[11:10], INPUT[5:4], INPUT[7:6], INPUT[1:0], INPUT[3:2]}
endmodule

// 2
module u_REV_SUB2 (
  input  [31:0] INPUT,
  input  SELECT,
  output [31:0] OUTPUT
);

  Multiplexer #(.width(32), .enable("false")) multiplexer_1 (
    .in0(INPUT),
    .in1({INPUT[27:24], INPUT[31:28], INPUT[19:16], INPUT[23:20], INPUT[11:8], INPUT[15:12], INPUT[3:0], INPUT[7:4]}),
    .out(OUTPUT), .sel(SELECT));

  // Other names for the same wires on the sheet: FWD[31:0] = INPUT;
  //   REV[31:0] = {INPUT[27:24], INPUT[31:28], INPUT[19:16], INPUT[23:20], INPUT[11:8], INPUT[15:12], INPUT[3:0], INPUT[7:4]}
endmodule

// 3
module u_REV_SUB3 (
  input  [31:0] INPUT,
  input  SELECT,
  output [31:0] OUTPUT
);

  Multiplexer #(.width(32), .enable("false")) multiplexer_1 (
    .in0(INPUT), .in1({INPUT[23:16], INPUT[31:24], INPUT[7:0], INPUT[15:8]}), .out(OUTPUT), .sel(SELECT));

  // Other names for the same wires on the sheet: FWD[31:0] = INPUT;
  //   REV[31:0] = {INPUT[23:16], INPUT[31:24], INPUT[7:0], INPUT[15:8]}
endmodule

// 4
module u_REV_SUB4 (
  input  [31:0] INPUT,
  input  SELECT,
  output [31:0] OUTPUT
);

  Multiplexer #(.width(32), .enable("false")) multiplexer_1 (
    .in0(INPUT), .in1({INPUT[15:0], INPUT[31:16]}), .out(OUTPUT), .sel(SELECT));

  // Other names for the same wires on the sheet: FWD[31:0] = INPUT; REV[31:0] = {INPUT[15:0], INPUT[31:16]}
endmodule

module u_SLA (
  input  [31:0] INPUT,
  input  [4:0] SHAMT,
  output [31:0] OUTPUT
);

  wire [31:0] shifter_1_out, u_rev_1_output;

  u_REV u_rev_1 (.INPUT(INPUT), .REVERSE_AMOUNT({5{1'b1}}), .OUTPUT(u_rev_1_output));
  Shifter #(.width(32), .shift("ar")) shifter_1 (.in(u_rev_1_output), .\dist (SHAMT), .out(shifter_1_out));
  u_REV u_rev_2 (.INPUT(shifter_1_out), .REVERSE_AMOUNT({5{1'b1}}), .OUTPUT(OUTPUT));
endmodule

module u_STU (
  input  [31:0] INPUT_A,
  input  [31:0] INPUT_B,
  output [31:0] OUTPUT
);


  assign OUTPUT = {INPUT_B[16:0], INPUT_A[14:0]};
endmodule

module u_DIV (
  input  NEGATIVE___X,
  input  [31:0] INPUT_A,
  input  [31:0] INPUT_B,
  input  POSITIVE___X,
  output [31:0] OUTPUT
);

  wire and_1_out, and_2_out, EQZ, GTZ, LTZ, xor_1_out;
  wire [31:0] adder_1_out, adder_2_out, adder_3_out, divider_1_out, INTERMEDIATE_DIV, multiplexer_1_out,
       multiplexer_2_out, multiplexer_3_out, not_1_out, not_2_out, not_3_out;

  // Probe on INPUT_A
  // Probe on INPUT_B
  assign not_1_out = ~INPUT_A;  // NOT_Gate not_1, 32 bits wide
  assign not_2_out = ~INPUT_B;  // NOT_Gate not_2, 32 bits wide
  and and_1 (and_1_out, POSITIVE___X, EQZ);
  Adder #(.width(32)) adder_1 (.a(not_1_out), .b(32'h1), .out(adder_1_out));  // open: cin, cout
  Comparator #(.width(32)) comparator_1 (.a({32{1'b0}}), .b(INPUT_B), .gt(LTZ), .eq(EQZ), .lt(GTZ));
  Adder #(.width(32)) adder_2 (.a(not_2_out), .b(32'h1), .out(adder_2_out));  // open: cin, cout
  Multiplexer #(.width(32), .enable("false")) multiplexer_1 (
    .in0(INTERMEDIATE_DIV), .in1(32'h7fffffff), .out(multiplexer_1_out), .sel(and_1_out));
  Multiplexer #(.width(32), .enable("false")) multiplexer_2 (
    .in0(INPUT_A), .in1(adder_1_out), .out(multiplexer_2_out), .sel(NEGATIVE___X));
  Multiplexer #(.width(32), .enable("false")) multiplexer_3 (
    .in0(INPUT_B), .in1(adder_2_out), .out(multiplexer_3_out), .sel(LTZ));
  and and_2 (and_2_out, NEGATIVE___X, EQZ);
  Divider #(.width(32)) divider_1 (
    .a(multiplexer_2_out), .b(multiplexer_3_out), .out(divider_1_out));  // open: upper, rem
  Multiplexer #(.width(32), .enable("false")) multiplexer_4 (
    .in0(multiplexer_1_out), .in1(32'h80000000), .out(OUTPUT), .sel(and_2_out));
  xor xor_1 (xor_1_out, NEGATIVE___X, LTZ);
  assign not_3_out = ~divider_1_out;  // NOT_Gate not_3, 32 bits wide
  // Probe on OUTPUT
  Adder #(.width(32)) adder_3 (.a(not_3_out), .b(32'h1), .out(adder_3_out));  // open: cin, cout
  Multiplexer #(.width(32), .enable("false")) multiplexer_5 (
    .in0(divider_1_out), .in1(adder_3_out), .out(INTERMEDIATE_DIV), .sel(xor_1_out));

  // Other names for the same wires on the sheet: NEG = NEGATIVE___X
endmodule

// DECODER
module u_DECODER (
  input  [31:0] INSTRUCTION_MEMORY_INPUT,
  output [4:0] RD,
  output [2:0] JC,
  output [16:0] IMMEDIATE,
  output [23:0] ADDRESS,
  output [4:0] RS,
  output [3:0] OP,
  output [4:0] RI,
  output I
);

  Bit_Extender #(.in_width(17), .out_width(5)) bit_extender_1 (.in(INSTRUCTION_MEMORY_INPUT[16:0]), .out(RI));

  assign ADDRESS = INSTRUCTION_MEMORY_INPUT[23:0];
  assign I = INSTRUCTION_MEMORY_INPUT[27];
  assign IMMEDIATE = INSTRUCTION_MEMORY_INPUT[16:0];
  assign JC = INSTRUCTION_MEMORY_INPUT[26:24];
  assign OP = INSTRUCTION_MEMORY_INPUT[31:28];
  assign RD = INSTRUCTION_MEMORY_INPUT[26:22];
  assign RS = INSTRUCTION_MEMORY_INPUT[21:17];

  // Other names for the same wires on the sheet: REM_INSTR[26:0] = INSTRUCTION_MEMORY_INPUT[26:0];
  //   JUMP_COND___JC[2:0] = INSTRUCTION_MEMORY_INPUT[26:24]; IMM_SELECTOR__I = INSTRUCTION_MEMORY_INPUT[27];
  //   OPCODE[3:0] = INSTRUCTION_MEMORY_INPUT[31:28]

  // Notes on the sheet:
  //   INPUT
  //   PROCESSING
  //   OUTPUTS
endmodule

// CONTROL
module u_CONTROLLER (
  input  [3:0] OPCODE,
  input  [2:0] JC,
  input  I,
  input  [31:0] JC_2,
  output [3:0] ALU_CONTROL,
  output ADDR_SEL,
  output [1:0] RD_SELECT,
  output WORD_MODE,
  output MEM_WRITE,
  output EN_WRITE,
  output JAL
);

  wire _1_2_XOR, and_1_out, and_2_out, and_5_out, comparator_1_eq, comparator_1_gt, comparator_1_lt,
       EN_SUB_WRITE, EQ_7, JRES, MEM_READ, not_1_out, not_2_out, not_3_out, or_1_out, or_2_out, or_3_out,
       or_4_out;
  wire [1:0] multiplexer_2_out, multiplexer_3_out;

  not not_1 (not_1_out, OPCODE[0]);
  and and_1 (and_1_out, not_1_out, OPCODE[3]);
  and and_2 (and_2_out, OPCODE[0], OPCODE[3]);
  or or_1 (or_1_out, OPCODE[1], OPCODE[2]);
  xor xor_1 (_1_2_XOR, OPCODE[1], OPCODE[2]);
  not not_2 (not_2_out, OPCODE[1]);
  and and_3 (WORD_MODE, OPCODE[3], not_2_out, OPCODE[2]);
  Multiplexer #(.enable("false")) multiplexer_1 (.in0(EN_SUB_WRITE), .in1(1'b1), .out(EN_WRITE), .sel(JAL));
  and and_4 (MEM_READ, _1_2_XOR, and_1_out);
  and and_5 (and_5_out, OPCODE[0], OPCODE[1], OPCODE[2], OPCODE[3]);
  nand nand_1 (EN_SUB_WRITE, and_2_out, or_1_out);
  and and_6 (MEM_WRITE, and_2_out, _1_2_XOR);
  and and_7 (JAL, EQ_7, and_5_out);
  and and_8 (ADDR_SEL, and_5_out, JRES);
  and and_9 (EQ_7, JC[0], JC[1], JC[2]);
  Multiplexer #(.width(2), .enable("false")) multiplexer_2 (
    .in0(2'b01), .in1(2'b00), .out(multiplexer_2_out), .sel(MEM_READ));
  Multiplexer #(.width(2), .enable("false")) multiplexer_3 (
    .in0(multiplexer_2_out), .in1(2'b10), .out(multiplexer_3_out), .sel(JAL));
  Comparator #(.width(32)) comparator_1 (
    .a(JC_2), .b({32{1'b0}}), .gt(comparator_1_gt), .eq(comparator_1_eq), .lt(comparator_1_lt));
  not not_3 (not_3_out, comparator_1_eq);
  Multiplexer #(.width(2), .enable("false")) multiplexer_4 (
    .in0(2'b11), .in1(multiplexer_3_out), .out(RD_SELECT), .sel(or_2_out));
  or or_2 (or_2_out, EN_WRITE, EQ_7);
  or or_3 (or_3_out, comparator_1_lt, comparator_1_eq);
  or or_4 (or_4_out, comparator_1_eq, comparator_1_gt);
  Multiplexer #(.select(3), .enable("false")) multiplexer_5 (
    .in0(1'b1), .in1(comparator_1_gt), .in2(comparator_1_eq), .in3(comparator_1_lt), .in4(or_3_out),
    .in5(not_3_out), .in6(or_4_out), .in7(EQ_7), .out(JRES), .sel(JC));

  assign ALU_CONTROL = OPCODE;

  // Other names for the same wires on the sheet: J_ADDR = ADDR_SEL; JC_t[31:0] = JC_2; M_WRITE = MEM_WRITE;
  //   OP[3:0] = OPCODE; R_SEL[1:0] = RD_SELECT; UNUSED = I; W_MODE = WORD_MODE

  // Notes on the sheet:
  //   INPUTS/OUTPUTS
  //   CONTROLLER
  //   I/O
endmodule
